# Fritzing sketch semiot-device (saved by Fritzing 0.9.1b)
breadboards: 1

parts:
  DHT11 = DHT11 Humitidy and Temperature Sensor
  R1 = Resistor [tolerance=±5% resistance=4.7k package=THT]
  WiFi_Module = ESP8266 WiFi Module [part_number=ESP8266]
  Arduino_Mega_2560 = Arduino Mega 2560 (Rev3)

nets:
  VDD: DHT11.VDD, R1.Pin_0, Arduino_Mega_2560.5V
  N1: DHT11.DATA, R1.Pin_1, Arduino_Mega_2560.D2_PWM
  GND: DHT11.GND, WiFi_Module.GND, Arduino_Mega_2560.GND
  N2: WiFi_Module.RXD, Arduino_Mega_2560.D14/TX3
  VCC: WiFi_Module.VCC, WiFi_Module.CH_PD, Arduino_Mega_2560.3V3
  N3: WiFi_Module.TXD, Arduino_Mega_2560.D15/RX3

custom parts:
  DHT11 Humitidy and Temperature Sensor: DHT11 Humidity and Temperature Sensor
  ESP8266 WiFi Module: Generic WiFi Module based on the ESP8266 with onboard PCB antenna and UART communications
